// Logisim project AOC2017.circ as structural Verilog: 5 circuits, main circuit day02b
module ssvTokenizer (
  input  [6:0] ASCII,
  input  Enable,
  input  Available,
  input  Clk,
  input  Rst,
  output TokenP,
  output NumberP,
  output SpaceP,
  output NewlineP,
  output [31:0] Number,
  output RST_2,
  output Read
);

  wire and_1_out, comparator_1_eq, comparator_2_eq, comparator_3_eq, HasNumber_q, nand_1_out;
  wire [31:0] adder_1_out, bit_extender_1_out, multiplexer_1_out, multiplier_1_out, Number_q;

  and and_1 (and_1_out, Enable, Available);
  and and_2 (Read, and_1_out, nand_1_out);
  nand nand_1 (nand_1_out, ~comparator_3_eq, HasNumber_q);  // NAND_Gate
  Comparator #(.width(7)) comparator_1 (.a(7'b0100000), .b(ASCII), .eq(comparator_1_eq));  // open: gt, lt
  Comparator #(.width(7)) comparator_2 (.a(7'b0001010), .b(ASCII), .eq(comparator_2_eq));  // open: gt, lt
  assign bit_extender_1_out = {{28{1'b0}}, ASCII[3:0]};  // Bit_Extender bit_extender_1
  Comparator #(.width(3)) comparator_3 (.a(ASCII[6:4]), .b(3'b011), .eq(comparator_3_eq));  // open: gt, lt
  D_Flip_Flop HasNumber (
    .clk(Clk), .D(comparator_3_eq), .Q(HasNumber_q), .en(and_1_out), .reset(Rst));  // open: Qn, preset
  and and_3 (NumberP, ~comparator_3_eq, HasNumber_q, Available);  // AND_Gate
  and and_4 (SpaceP, comparator_1_eq, ~HasNumber_q, Available);  // AND_Gate
  and and_5 (NewlineP, comparator_2_eq, ~HasNumber_q, Available);  // AND_Gate
  Multiplier #(.width(32)) multiplier_1 (.a(Number_q), .b(32'ha), .out(multiplier_1_out));  // open: cin, cout
  or or_1 (TokenP, NumberP, SpaceP, NewlineP);
  Multiplexer #(.width(32), .enable("false")) multiplexer_1 (
    .in0({32{1'b0}}), .in1(adder_1_out), .out(multiplexer_1_out), .sel(comparator_3_eq));
  Adder #(.width(32)) adder_1 (.a(bit_extender_1_out), .b(multiplier_1_out), .out(adder_1_out));  // open: cin, cout
  Register #(.width(32)) u_Number (.D(multiplexer_1_out), .en(and_1_out), .Q(Number_q), .clk(Clk), .clr(Rst));
  assign Number = NumberP ? Number_q : 32'bz;  // Controlled_Buffer controlled_buffer_1

  assign RST_2 = Rst;

  // Notes on the sheet:
  //   Enable: pull=up
endmodule

module day01a (
  input  RST,
  output [31:0] Result
);

  wire clock_1_out, comparator_1_eq, comparator_2_eq, j_k_ff_1_qn, keyboard_1_avail;
  wire [3:0] bit_extender_1_out, Fst_q, Last_q, SndLast_q;
  wire [6:0] keyboard_1_data;
  wire [31:0] adder_1_out, and_1_out, bit_extender_2_out, bit_extender_3_out, bit_extender_4_out, Subtotal_q;

  Keyboard keyboard_1 (.clk(clock_1_out), .clr(RST), .avail(keyboard_1_avail), .data(keyboard_1_data));  // open: re
  Clock clock_1 (.out(clock_1_out));
  Bit_Extender #(.in_width(7), .out_width(4)) bit_extender_1 (.in(keyboard_1_data), .out(bit_extender_1_out));
  J_K_Flip_Flop j_k_ff_1 (
    .J(keyboard_1_avail), .clk(clock_1_out), .K(1'b0), .Qn(j_k_ff_1_qn), .en(1'b1), .reset(RST));  // open: Q, preset
  Register #(.width(4)) Last (.D(bit_extender_1_out), .en(keyboard_1_avail), .Q(Last_q), .clk(clock_1_out), .clr(RST));
  Register #(.width(4)) SndLast (.D(Last_q), .en(keyboard_1_avail), .Q(SndLast_q), .clk(clock_1_out), .clr(RST));
  Register #(.width(4)) Fst (.D(bit_extender_1_out), .en(j_k_ff_1_qn), .Q(Fst_q), .clk(clock_1_out), .clr(RST));
  assign bit_extender_2_out = {{28{1'b0}}, Last_q};  // Bit_Extender bit_extender_2
  Comparator #(.width(4)) comparator_1 (.a(Last_q), .b(SndLast_q), .eq(comparator_1_eq));  // open: gt, lt
  Comparator #(.width(4)) comparator_2 (.a(Last_q), .b(Fst_q), .eq(comparator_2_eq));  // open: gt, lt
  assign bit_extender_3_out = {{28{1'b0}}, Fst_q};  // Bit_Extender bit_extender_3
  Adder #(.width(32)) adder_1 (.a(bit_extender_2_out), .b(Subtotal_q), .out(adder_1_out));  // open: cin, cout
  assign bit_extender_4_out = {{31{1'b0}}, comparator_2_eq};  // Bit_Extender bit_extender_4
  assign and_1_out = bit_extender_4_out & bit_extender_3_out;  // AND_Gate and_1, 32 bits wide
  Register #(.width(32)) Subtotal (.D(adder_1_out), .en(comparator_1_eq), .Q(Subtotal_q), .clk(clock_1_out), .clr(RST));
  Adder #(.width(32)) adder_2 (.a(Subtotal_q), .b(and_1_out), .out(Result));  // open: cin, cout
  // Probe on Result
endmodule

module day01b (
  input  RST,
  output [31:0] Result
);

  wire and_1_out, and_2_out, clock_1_out, comparator_1_eq, comparator_2_eq, keyboard_1_avail, not_1_out,
       not_2_out, not_3_out, or_1_out, t_ff_1_q;
  wire [3:0] bit_extender_1_out, controlled_buffer_1_out, register_1_q, register_2_q;
  wire [6:0] keyboard_1_data;
  wire [23:0] adder_1_out, controlled_buffer_2_out, counter_1_q, counter_2_q, shifter_1_out;
  wire [31:0] adder_2_out, bit_extender_2_out, Subtotal_q;

  Keyboard keyboard_1 (.clk(clock_1_out), .clr(RST), .avail(keyboard_1_avail), .data(keyboard_1_data));  // open: re
  Clock clock_1 (.out(clock_1_out));
  Bit_Extender #(.in_width(7), .out_width(4)) bit_extender_1 (.in(keyboard_1_data), .out(bit_extender_1_out));
  assign controlled_buffer_1_out = keyboard_1_avail ? bit_extender_1_out : 4'bz;  // Controlled_Buffer controlled_buffer_1
  Counter #(.width(24), .max('hffffff)) counter_1 (
    .count(keyboard_1_avail), .Q(counter_1_q), .clk(clock_1_out), .clr(RST));  // open: load, D, carry
  assign controlled_buffer_2_out = keyboard_1_avail ? counter_1_q : 24'bz;  // Controlled_Buffer controlled_buffer_2
  Shifter #(.width(24), .shift("lr")) shifter_1 (.in(counter_1_q), .\dist (5'b00001), .out(shifter_1_out));
  RAM #(.addrWidth(24), .dataWidth(4)) ram_1 (
    .addr(controlled_buffer_2_out), .data(controlled_buffer_1_out), .sel(1'b1), .clk(clock_1_out),
    .ld(not_1_out), .clr(RST));
  not not_1 (not_1_out, keyboard_1_avail);
  T_Flip_Flop t_ff_1 (.clk(clock_1_out), .T(1'b1), .Q(t_ff_1_q), .reset(or_1_out));  // open: Qn, preset, en
  or or_1 (or_1_out, keyboard_1_avail, RST);
  Counter #(.width(24), .max('hffffff)) counter_2 (
    .count(t_ff_1_q), .Q(counter_2_q), .clk(clock_1_out), .clr(or_1_out));  // open: load, D, carry
  Comparator #(.width(24)) comparator_1 (.a(counter_2_q), .b(shifter_1_out), .eq(comparator_1_eq));  // open: gt, lt
  Adder #(.width(24)) adder_1 (.a(shifter_1_out), .b(counter_2_q), .out(adder_1_out));  // open: cin, cout
  Multiplexer #(.width(24)) multiplexer_1 (
    .in0(adder_1_out), .in1(counter_2_q), .out(controlled_buffer_2_out), .sel(t_ff_1_q), .en(not_2_out));
  not not_2 (not_2_out, or_1_out);
  and and_1 (and_1_out, comparator_1_eq, t_ff_1_q);
  Register #(.width(4)) register_1 (
    .D(controlled_buffer_1_out), .en(t_ff_1_q), .Q(register_1_q), .clk(clock_1_out), .clr(or_1_out));
  Register #(.width(4)) register_2 (
    .D(controlled_buffer_1_out), .en(not_3_out), .Q(register_2_q), .clk(clock_1_out), .clr(or_1_out));
  not not_3 (not_3_out, t_ff_1_q);
  assign bit_extender_2_out = {{28{1'b0}}, register_1_q};  // Bit_Extender bit_extender_2
  Comparator #(.width(4)) comparator_2 (.a(register_1_q), .b(register_2_q), .eq(comparator_2_eq));  // open: gt, lt
  Adder #(.width(32)) adder_2 (.a(Subtotal_q), .b(bit_extender_2_out), .out(adder_2_out));  // open: cin, cout
  and and_2 (and_2_out, comparator_2_eq, ~t_ff_1_q);  // AND_Gate
  Register #(.width(32)) register_3 (.D(Subtotal_q), .en(and_1_out), .Q(Result), .clk(clock_1_out), .clr(or_1_out));
  Register #(.width(32)) Subtotal (.D(adder_2_out), .en(and_2_out), .Q(Subtotal_q), .clk(clock_1_out), .clr(or_1_out));
  // Probe on Result
endmodule

// 8
module day02a (
  input  RST,
  output [31:0] Result
);

  wire clock_1_out, comparator_1_lt, comparator_2_gt, d_ff_1_q, keyboard_1_avail, not_1_out, or_1_out,
       ssvtokenizer_1_newlinep, ssvtokenizer_1_numberp, ssvtokenizer_1_read, ssvtokenizer_1_rst_2;
  wire [1:0] priority_encoder_1_out, priority_encoder_2_out;
  wire [6:0] keyboard_1_data;
  wire [31:0] adder_1_out, Max_q, Min_q, multiplexer_1_out, multiplexer_2_out, ssvtokenizer_1_number,
       subtractor_1_out;

  Keyboard keyboard_1 (
    .clk(clock_1_out), .re(ssvtokenizer_1_read), .clr(ssvtokenizer_1_rst_2), .avail(keyboard_1_avail),
    .data(keyboard_1_data));
  ssvTokenizer ssvtokenizer_1 (
    .ASCII(keyboard_1_data), .Available(keyboard_1_avail), .Clk(clock_1_out), .Rst(RST),
    .Read(ssvtokenizer_1_read), .NumberP(ssvtokenizer_1_numberp), .NewlineP(ssvtokenizer_1_newlinep),
    .Number(ssvtokenizer_1_number), .RST_2(ssvtokenizer_1_rst_2));  // open: TokenP, SpaceP, Enable
  Clock clock_1 (.out(clock_1_out));
  D_Flip_Flop d_ff_1 (.clk(clock_1_out), .D(RST), .Q(d_ff_1_q), .preset(RST));  // open: Qn, en, reset
  or or_1 (or_1_out, d_ff_1_q, ssvtokenizer_1_newlinep);
  not not_1 (not_1_out, ssvtokenizer_1_numberp);
  Comparator #(.width(32), .mode("unsigned")) comparator_1 (
    .a(Max_q), .b(ssvtokenizer_1_number), .lt(comparator_1_lt));  // open: gt, eq
  Comparator #(.width(32), .mode("unsigned")) comparator_2 (
    .a(Min_q), .b(ssvtokenizer_1_number), .gt(comparator_2_gt));  // open: eq, lt
  Multiplexer #(.select(2), .width(32), .enable("false")) multiplexer_1 (
    .in0(Max_q), .in1(ssvtokenizer_1_number), .in2(Max_q), .in3({32{1'b0}}), .out(multiplexer_1_out),
    .sel(priority_encoder_1_out));
  Priority_Encoder #(.select(2), .disabled(0)) priority_encoder_1 (
    .in0(1'b1), .in1(comparator_1_lt), .in2(not_1_out), .in3(or_1_out), .out(priority_encoder_1_out));  // open: gs, en_out, en_in
  Multiplexer #(.select(2), .width(32), .enable("false")) multiplexer_2 (
    .in0(Min_q), .in1(ssvtokenizer_1_number), .in2(Min_q), .in3({32{1'b1}}), .out(multiplexer_2_out),
    .sel(priority_encoder_2_out));
  Priority_Encoder #(.select(2), .disabled(0)) priority_encoder_2 (
    .in0(1'b1), .in1(comparator_2_gt), .in2(not_1_out), .in3(or_1_out), .out(priority_encoder_2_out));  // open: gs, en_out, en_in
  Register #(.width(32)) Max (.D(multiplexer_1_out), .Q(Max_q), .clk(clock_1_out), .clr(RST));  // open: en
  Register #(.width(32)) Min (.D(multiplexer_2_out), .Q(Min_q), .clk(clock_1_out), .clr(RST));  // open: en
  Adder #(.width(32)) adder_1 (.a(Result), .b(subtractor_1_out), .out(adder_1_out));  // open: cin, cout
  Subtractor #(.width(32)) subtractor_1 (.a(Max_q), .b(Min_q), .out(subtractor_1_out));  // open: bin, bout
  Register #(.width(32)) Subtotal (
    .D(adder_1_out), .en(ssvtokenizer_1_newlinep), .Q(Result), .clk(clock_1_out), .clr(RST));
  // Probe on Result
endmodule

module day02b (
  input  RST,
  output [31:0] Result
);

  wire clock_1_out, comparator_2_eq, comparator_3_eq, keyboard_1_avail, not_1_out, or_1_out,
       priority_encoder_1_p2, priority_encoder_1_p5, ssvtokenizer_1_newlinep, ssvtokenizer_1_numberp,
       ssvtokenizer_1_read, ssvtokenizer_1_rst_2;
  wire [1:0] priority_encoder_1_p3, register_1_q, rom_1_data, rom_1_data_4;
  wire [4:0] rom_1_data_3;
  wire [4:2] rom_1_data_2;
  wire [6:0] keyboard_1_data;
  wire [23:0] controlled_buffer_2_out, Id_q, In_q, Iread_q, subtractor_1_out;
  wire [31:0] adder_1_out, controlled_buffer_1_out, d_q, divider_1_out, divider_1_rem, ssvtokenizer_1_number;

  Clock clock_1 (.out(clock_1_out));
  Keyboard keyboard_1 (
    .clk(clock_1_out), .re(ssvtokenizer_1_read), .clr(ssvtokenizer_1_rst_2), .avail(keyboard_1_avail),
    .data(keyboard_1_data));
  ssvTokenizer ssvtokenizer_1 (
    .ASCII(keyboard_1_data), .Available(keyboard_1_avail), .Clk(clock_1_out), .Rst(RST),
    .Read(ssvtokenizer_1_read), .NumberP(ssvtokenizer_1_numberp), .NewlineP(ssvtokenizer_1_newlinep),
    .Number(ssvtokenizer_1_number), .RST_2(ssvtokenizer_1_rst_2), .Enable(rom_1_data_4[1]));  // open: TokenP, SpaceP
  assign controlled_buffer_1_out = rom_1_data_4[1] ? ssvtokenizer_1_number : 32'bz;  // Controlled_Buffer controlled_buffer_1
  assign controlled_buffer_2_out = rom_1_data_4[1] ? Iread_q : 24'bz;  // Controlled_Buffer controlled_buffer_2
  Counter #(.width(24), .max('hffffff)) Iread (
    .load(rom_1_data_4[0]), .count(ssvtokenizer_1_numberp), .Q(Iread_q), .clk(clock_1_out), .clr(RST));  // open: D, carry
  or or_1 (or_1_out, ssvtokenizer_1_numberp, not_1_out);
  not not_1 (not_1_out, rom_1_data_4[1]);
  // Priority_Encoder #(.select(2)) priority_encoder_1: pin names not known; wires that end beside it: 1'b1, priority_encoder_1_p2, priority_encoder_1_p3, ssvtokenizer_1_newlinep, priority_encoder_1_p5
  Subtractor #(.width(24)) subtractor_1 (.a(Iread_q), .b(24'h1), .out(subtractor_1_out));  // open: bin, bout
  RAM #(.addrWidth(24), .dataWidth(32)) ram_1 (
    .addr(controlled_buffer_2_out), .data(controlled_buffer_1_out), .sel(or_1_out), .clk(clock_1_out),
    .ld(not_1_out), .clr(RST));
  Register #(.width(2)) register_1 (.D(rom_1_data), .Q(register_1_q), .clk(clock_1_out), .clr(RST));  // open: en
  // Probe on {register_1_q, priority_encoder_1_p3}
  // Probe on controlled_buffer_1_out
  Register #(.width(32)) d (.D(controlled_buffer_1_out), .en(rom_1_data_3[4]), .Q(d_q), .clk(clock_1_out), .clr(RST));
  Counter #(.width(24), .max('hffffff)) In (
    .load(rom_1_data_3[3]), .count(rom_1_data_3[2]), .Q(In_q), .clk(clock_1_out), .clr(RST));  // open: D, carry
  Counter #(.width(24), .max('hffffff)) Id (
    .load(rom_1_data_3[1]), .count(rom_1_data_3[0]), .Q(Id_q), .clk(clock_1_out), .clr(RST));  // open: D, carry
  ROM #(.addrWidth(4), .dataWidth(12)) rom_1 (
    .addr({register_1_q, priority_encoder_1_p3}),
    .data({rom_1_data_4, rom_1_data_3, rom_1_data_2, rom_1_data}));  // open: sel
  // Probe on {rom_1_data_4, rom_1_data_3, rom_1_data_2, rom_1_data}
  Divider #(.width(32)) divider_1 (
    .a(controlled_buffer_1_out), .b(d_q), .out(divider_1_out), .rem(divider_1_rem));  // open: upper
  Comparator #(.width(24)) comparator_1 (.a(subtractor_1_out), .b(In_q), .eq(priority_encoder_1_p2));  // open: gt, lt
  assign controlled_buffer_2_out = rom_1_data_2[3] ? In_q : 24'bz;  // Controlled_Buffer controlled_buffer_3
  Comparator #(.width(24)) comparator_2 (.a(In_q), .b(Id_q), .eq(comparator_2_eq));  // open: gt, lt
  assign controlled_buffer_2_out = rom_1_data_2[4] ? Id_q : 24'bz;  // Controlled_Buffer controlled_buffer_4
  Adder #(.width(32)) adder_1 (.a(divider_1_out), .b(Result), .out(adder_1_out));  // open: cin, cout
  Comparator #(.width(32)) comparator_3 (.a({32{1'b0}}), .b(divider_1_rem), .eq(comparator_3_eq));  // open: gt, lt
  and and_1 (priority_encoder_1_p5, ~comparator_2_eq, comparator_3_eq);  // AND_Gate
  Register #(.width(32)) Subtotal (.D(adder_1_out), .en(rom_1_data_2[2]), .Q(Result), .clk(clock_1_out), .clr(RST));
  // Probe on Result

  // Notes on the sheet:
  //   contents of rom_1 (hex, n*v repeats v):
  //   940 940 942 803 89 12a b 54c 311 13 13 13 4*3
endmodule
